# Fritzing sketch schematic (saved by Fritzing 1.0.3b)
breadboards: 1

parts:
  Arduino_D1_(Wemos)_D1_R1 = Arduino Uno (Rev3) - ICSP
  V1 = DC Power [voltage=12V internal_resistance=0.1Ω]
  CD74HC4067 = Analog Digital MUX Breakout
  Crane_Rotator = Basic Servo
  Crane_Up/Down = Basic Servo
  Crane_Extender?? = Basic Servo
  Electromagnet = Inductor [package="400 mil [THT]"]
  Q1 = NPN-Transistor [package="TO92 [THT]"]
  R1 = Resistor [tolerance=±5% power=0.25W resistance=220 package=THT]
  R2 = Resistor [tolerance=±5% power=0.25W resistance=220 package=THT]
  R3 = Resistor [tolerance=±5% power=0.25W resistance=220 package=THT]
  R4 = Resistor [tolerance=±5% power=0.25W resistance=220 package=THT]
  R5 = Resistor [tolerance=±5% power=0.25W resistance=220 package=THT]
  R6 = Resistor [tolerance=±5% power=0.25W resistance=220 package=THT]
  R7 = Resistor [tolerance=±5% power=0.25W resistance=220 package=THT]
  R8 = Resistor [tolerance=±5% power=0.25W resistance=220 package=THT]
  R9 = Resistor [tolerance=±5% power=0.25W resistance=220 package=THT]

nets:
  N1: Arduino_D1_(Wemos)_D1_R1.A0, CD74HC4067.SIG
  GND: Arduino_D1_(Wemos)_D1_R1.GND, V1.V-, CD74HC4067.GND, CD74HC4067.EN, Crane_Rotator.gnd, Crane_Up/Down.gnd, Crane_Extender??.gnd, Electromagnet.pin_0
  N2: Arduino_D1_(Wemos)_D1_R1.D8, CD74HC4067.S0
  N3: Arduino_D1_(Wemos)_D1_R1.D9_PWM, CD74HC4067.S1
  N4: Arduino_D1_(Wemos)_D1_R1.D10_PWM/SS, CD74HC4067.S2
  N5: Arduino_D1_(Wemos)_D1_R1.D11_PWM/MOSI, CD74HC4067.S3
  N6: Arduino_D1_(Wemos)_D1_R1.D0/RX, Q1.B
  N7: Arduino_D1_(Wemos)_D1_R1.D2, Crane_Rotator.pulse
  N8: Arduino_D1_(Wemos)_D1_R1.D3_PWM, Crane_Up/Down.pulse
  N9: Arduino_D1_(Wemos)_D1_R1.D4, Crane_Extender??.pulse
  12V: Arduino_D1_(Wemos)_D1_R1.VIN, V1.V+, Q1.C
  N10: CD74HC4067.C0, R1.Pin_1
  N11: CD74HC4067.C1, R2.Pin_1
  N12: CD74HC4067.C2, R3.Pin_1
  N13: CD74HC4067.C3, R4.Pin_1
  N14: CD74HC4067.C4, R5.Pin_1
  N15: CD74HC4067.C5, R6.Pin_1
  N16: CD74HC4067.C6, R7.Pin_1
  N17: CD74HC4067.C7, R8.Pin_1
  N18: CD74HC4067.C8, R9.Pin_1
  5V: CD74HC4067.VCC, Crane_Rotator.vcc, Crane_Up/Down.vcc, Crane_Extender??.vcc, R1.Pin_0, R2.Pin_0, R3.Pin_0, R4.Pin_0, R5.Pin_0, R6.Pin_0, R7.Pin_0, R8.Pin_0, R9.Pin_0
  N19: Electromagnet.pin_1, Q1.E

notes:
  The resistors come from the game pieces. So if no piece is placed on a square it will not be there.
  The resistance will vary depending on the piece placed.
